# Fritzing sketch Breadboard (saved by Fritzing 0.9.9b)
stripboards: 1

parts:
  U1 = 74HC595 [package="DIP16 [THT]"]
  IC1 = Microchip MCP23008 8-bit I/O expander [part_number=MCP23008 package="DIP (Dual Inline) [THT]"]

nets:
  GND: U1.GND, U1.OE, IC1.A2, IC1.A1, IC1.A0, IC1.VSS
  N1: U1.Q7', U1.DS
  VCC: U1.VCC, IC1.Reset, IC1.VDD

custom parts:
  Microchip MCP23008 8-bit I/O expander: Provides 8-bit, general purpose, parallel I/O expansion for I2C bus. Datasheet: http://ww1.microchip.com/downloads/en/devicedoc/21919e.pdf
